# Fritzing sketch basic_working_circuit (saved by Fritzing 0.9.3b)
breadboards: 1

parts:
  U2 = 74HC4051 [package=so16]
  U3 = 74HC4051 [package=so16]
  Part1 = Arduino Uno (Rev3)
  R1 = Resistor [tolerance=±5% resistance=10k package=THT]

nets:
  N1: U2.IO4, U3.IO4
  N2: U2.IO6, U3.IO6
  N3: U2.IO, Part1.D9_PWM, R1.Pin_0
  N4: U2.IO7, U3.IO7
  N5: U2.IO5, U3.IO5
  VSS: U2.INH, U2.VEE, U2.VSS, U3.INH, U3.VEE, U3.VSS, Part1.GND, R1.Pin_1
  N6: U2.C, Part1.D8
  N7: U2.B, Part1.D7
  N8: U2.A, Part1.D6_PWM
  N9: U2.IO3, U3.IO3
  N10: U2.IO0, U3.IO0
  N11: U2.IO1, U3.IO1
  N12: U2.IO2, U3.IO2
  VDD: U2.VDD, U3.VDD, Part1.5V
  N13: U3.IO, Part1.D5_PWM
  N14: U3.C, Part1.D4
  N15: U3.B, Part1.D3_PWM
  N16: U3.A, Part1.D2
