# Fritzing sketch midi_input_test (saved by Fritzing 0.9.3b)
breadboards: 1

parts:
  U1 = Optocoupler [package=THT]
  R1 = Resistor [tolerance=±20% resistance=470 package="0805 [SMD]"]
  Part1 = Arduino Uno (Rev3)
  D1 = Rectifier Diode [part_number=1N4001 package="300 mil [THT]"]
  R2 = Resistor [tolerance=±5% resistance=220 package="0603 [SMD]"]
  MIDI_socket_seen_from_behind = DIN-5 jack (MIDI) [package=THT]

nets:
  N1: U1.Pin_1, D1.cathode, MIDI_socket_seen_from_behind.5
  N2: U1.Pin_2, D1.anode, R2.Pin_0
  N3: U1.Pin_4, Part1.GND
  N4: U1.Pin_5, R1.Pin_1, Part1.D0/RX
  N5: R1.Pin_0, Part1.5V
  N6: R2.Pin_1, MIDI_socket_seen_from_behind.4
