# Fritzing sketch top_shelf_circuit (saved by Fritzing 0.9.3b)
breadboards: 4

parts:
  IC1 = DIP - 16 pins [chip_label="4051 (write)" package="DIP (Dual Inline) [THT]"]
  IC2 = DIP - 16 pins [chip_label="4051 (read)" package="DIP (Dual Inline) [THT]"]
  IC3 = DIP - 16 pins [chip_label="4051 (write)" package="DIP (Dual Inline) [THT]"]
  IC4 = DIP - 16 pins [chip_label="4051 (read)" package="DIP (Dual Inline) [THT]"]
  IC5 = DIP - 16 pins [chip_label="4051 (knobs)" package="DIP (Dual Inline) [THT]"]
  IC6 = DIP - 16 pins [chip_label="4051 (selector)" package="DIP (Dual Inline) [THT]"]
  R1 = Resistor [tolerance=±5% resistance=10k package=THT]
  R2 = Resistor [tolerance=±5% resistance=10k package=THT]
  Part1 = Arduino Mega 2560 (Rev3)
  IC7 = DIP - 16 pins [chip_label="4051 (write)" package="DIP (Dual Inline) [THT]"]
  IC8 = DIP - 16 pins [chip_label="4051 (write)" package="DIP (Dual Inline) [THT]"]
  IC9 = DIP - 16 pins [chip_label="4051 (read)" package="DIP (Dual Inline) [THT]"]
  IC10 = DIP - 16 pins [chip_label="4051 (read)" package="DIP (Dual Inline) [THT]"]
  IC11 = DIP - 16 pins [chip_label="4051 (knobs)" package="DIP (Dual Inline) [THT]"]
  R3 = Resistor [tolerance=±5% resistance=10k package=THT]
  R4 = Resistor [tolerance=±5% resistance=10k package=THT]
  TRS1 = Audio Jack (TRS) 3.5mm [package="PG203J [THT]"]
  TRS2 = Audio Jack (TRS) 3.5mm [package="PG203J [THT]"]
  TRS3 = Audio Jack (TRS) 3.5mm [package="PG203J [THT]"]
  TRS4 = Audio Jack (TRS) 3.5mm [package="PG203J [THT]"]
  R5 = Rotary Potentiometer (Large) [maximum_resistance=10kΩ package=THT]
  R6 = Rotary Potentiometer (Large) [maximum_resistance=10kΩ package=THT]
  R7 = Rotary Potentiometer (Large) [maximum_resistance=10kΩ package=THT]
  S2 = Taiway 100-SP-X-T1 SPDT Miniature Toggle Switch [part_number=100-SP-X-T1-0-0-B1-M1 package=THT]
  R8 = Resistor [tolerance=±5% resistance=10k package=THT]
  R9 = Resistor [tolerance=±5% resistance=10k package=THT]
  IC12 = DIP - 16 pins [chip_label="4051 (write)" package="DIP (Dual Inline) [THT]"]
  IC13 = DIP - 16 pins [chip_label="4051 (write)" package="DIP (Dual Inline) [THT]"]
  IC14 = DIP - 16 pins [chip_label="4051 (read)" package="DIP (Dual Inline) [THT]"]
  IC15 = DIP - 16 pins [chip_label="4051 (read)" package="DIP (Dual Inline) [THT]"]
  IC16 = DIP - 16 pins [chip_label="4051 (knobs)" package="DIP (Dual Inline) [THT]"]
  R10 = Resistor [tolerance=±5% resistance=10k package=THT]
  R11 = Resistor [tolerance=±5% resistance=10k package=THT]
  IC18 = DIP - 16 pins [chip_label="4051 (write)" package="DIP (Dual Inline) [THT]"]
  IC19 = DIP - 16 pins [chip_label="4051 (write)" package="DIP (Dual Inline) [THT]"]
  IC20 = DIP - 16 pins [chip_label="4051 (read)" package="DIP (Dual Inline) [THT]"]
  IC21 = DIP - 16 pins [chip_label="4051 (read)" package="DIP (Dual Inline) [THT]"]
  IC22 = DIP - 16 pins [chip_label="4051 (knobs)" package="DIP (Dual Inline) [THT]"]
  R12 = Resistor [tolerance=±5% resistance=10k package=THT]
  R13 = Resistor [tolerance=±5% resistance=10k package=THT]
  IC23 = DIP - 16 pins [chip_label="4051 (knobs)" package="DIP (Dual Inline) [THT]"]

nets:
  N1: IC1.pin1, IC2.pin1
  N2: IC1.pin2, IC2.pin2
  N3: IC1.pin3, IC6.pin1
  N4: IC1.pin4, IC2.pin4
  N5: IC1.pin5, IC2.pin5
  N6: IC1.pin6, IC1.pin7, IC1.pin8, IC2.pin6, IC2.pin7, IC2.pin8, IC3.pin6, IC3.pin7, IC3.pin8, IC4.pin6, IC4.pin7, IC4.pin8, IC5.pin6, IC5.pin7, IC5.pin8, IC6.pin6, IC6.pin7, IC6.pin8, R1.Pin_1, R2.Pin_1, Part1.GND, IC7.pin6, IC7.pin7, IC7.pin8, IC8.pin6, IC8.pin7, IC8.pin8, IC9.pin6, IC9.pin7, IC9.pin8, IC10.pin6, IC10.pin7, IC10.pin8, IC11.pin6, IC11.pin7, IC11.pin8, R3.Pin_1, R4.Pin_1, R5.leg2, R6.leg2, R7.leg2, R8.Pin_0, R9.Pin_0, IC12.pin6, IC12.pin7, IC12.pin8, IC13.pin6, IC13.pin7, IC13.pin8, IC14.pin6, IC14.pin7, IC14.pin8, IC15.pin6, IC15.pin7, IC15.pin8, IC16.pin6, IC16.pin7, IC16.pin8, R10.Pin_1, R11.Pin_1, IC18.pin6, IC18.pin7, IC18.pin8, IC19.pin6, IC19.pin7, IC19.pin8, IC20.pin6, IC20.pin7, IC20.pin8, IC21.pin6, IC21.pin7, IC21.pin8, IC22.pin6, IC22.pin7, IC22.pin8, R12.Pin_1, R13.Pin_1, IC23.pin6, IC23.pin7, IC23.pin8
  N7: IC1.pin9, IC3.pin9, Part1.D5_PWM, IC7.pin9, IC8.pin9, IC12.pin9, IC13.pin9, IC18.pin9, IC19.pin9
  N8: IC1.pin10, IC3.pin10, Part1.D6_PWM, IC7.pin10, IC8.pin10, IC12.pin10, IC13.pin10, IC18.pin10, IC19.pin10
  N9: IC1.pin11, IC3.pin11, Part1.D7_PWM, IC7.pin11, IC8.pin11, IC12.pin11, IC13.pin11, IC18.pin11, IC19.pin11
  N10: IC1.pin12, IC2.pin12, TRS3.Tip
  N11: IC1.pin13, IC2.pin13, TRS4.Tip
  N12: IC1.pin14, IC2.pin14, TRS2.Tip
  N13: IC1.pin15, IC2.pin15, TRS1.Tip
  N14: IC1.pin16, IC2.pin16, IC3.pin16, IC4.pin16, IC5.pin16, IC6.pin3, IC6.pin16, Part1.5V, IC7.pin16, IC8.pin16, IC9.pin16, IC10.pin16, IC11.pin16, R5.leg1, R6.leg1, R7.leg1, S2.COM, IC12.pin16, IC13.pin16, IC14.pin16, IC15.pin16, IC16.pin16, IC18.pin16, IC19.pin16, IC20.pin16, IC21.pin16, IC22.pin16, IC23.pin16
  N15: IC2.pin3, R1.Pin_0, Part1.D22
  N16: IC2.pin9, IC4.pin9, IC5.pin9, Part1.D2_PWM, IC9.pin9, IC10.pin9, IC11.pin9, IC14.pin9, IC15.pin9, IC16.pin9, IC20.pin9, IC21.pin9, IC22.pin9
  N17: IC2.pin10, IC4.pin10, IC5.pin10, Part1.D3_PWM, IC9.pin10, IC10.pin10, IC11.pin10, IC14.pin10, IC15.pin10, IC16.pin10, IC20.pin10, IC21.pin10, IC22.pin10
  N18: IC2.pin11, IC4.pin11, IC5.pin11, Part1.D4_PWM, IC9.pin11, IC10.pin11, IC11.pin11, IC14.pin11, IC15.pin11, IC16.pin11, IC20.pin11, IC21.pin11, IC22.pin11
  N19: IC3.pin1, IC4.pin1
  N20: IC3.pin2, IC4.pin2
  N21: IC3.pin3, IC6.pin2
  N22: IC3.pin4, IC4.pin4
  N23: IC3.pin5, IC4.pin5
  N24: IC3.pin12, IC4.pin12
  N25: IC3.pin13, IC4.pin13
  N26: IC3.pin14, IC4.pin14
  N27: IC3.pin15, IC4.pin15
  N28: IC4.pin3, R2.Pin_0, Part1.D23
  N29: IC5.pin3, Part1.A0
  N30: IC5.pin13, R7.wiper
  N31: IC5.pin14, R6.wiper
  N32: IC5.pin15, R5.wiper
  N33: IC6.pin4, IC8.pin3
  N34: IC6.pin5, IC7.pin3
  N35: IC6.pin9, Part1.D8_PWM
  N36: IC6.pin10, Part1.D9_PWM
  N37: IC6.pin11, Part1.D10_PWM
  N38: IC6.pin12, IC18.pin3
  N39: IC6.pin13, IC19.pin3
  N40: IC6.pin14, IC12.pin3
  N41: IC6.pin15, IC13.pin3
  N42: Part1.A1, IC11.pin3
  N43: Part1.A2, IC16.pin3
  N44: Part1.A3, IC23.pin3
  N45: Part1.D12_PWM, S2.L2, R8.Pin_1
  N46: Part1.D11_PWM, S2.L1, R9.Pin_1
  N47: Part1.D24, IC10.pin3, R3.Pin_0
  N48: Part1.D25, IC9.pin3, R4.Pin_0
  N49: IC7.pin1, IC9.pin1
  N50: IC7.pin2, IC9.pin2
  N51: IC7.pin4, IC9.pin4
  N52: IC7.pin5, IC9.pin5
  N53: IC7.pin12, IC9.pin12
  N54: IC7.pin13, IC9.pin13
  N55: IC7.pin14, IC9.pin14
  N56: IC7.pin15, IC9.pin15
  N57: IC8.pin1, IC10.pin1
  N58: IC8.pin2, IC10.pin2
  N59: IC8.pin4, IC10.pin4
  N60: IC8.pin5, IC10.pin5
  N61: IC8.pin12, IC10.pin12
  N62: IC8.pin13, IC10.pin13
  N63: IC8.pin14, IC10.pin14
  N64: IC8.pin15, IC10.pin15
  N65: IC12.pin1, IC14.pin1
  N66: IC12.pin2, IC14.pin2
  N67: IC12.pin4, IC14.pin4
  N68: IC12.pin5, IC14.pin5
  N69: IC12.pin12, IC14.pin12
  N70: IC12.pin13, IC14.pin13
  N71: IC12.pin14, IC14.pin14
  N72: IC12.pin15, IC14.pin15
  N73: IC13.pin1, IC15.pin1
  N74: IC13.pin2, IC15.pin2
  N75: IC13.pin4, IC15.pin4
  N76: IC13.pin5, IC15.pin5
  N77: IC13.pin12, IC15.pin12
  N78: IC13.pin13, IC15.pin13
  N79: IC13.pin14, IC15.pin14
  N80: IC13.pin15, IC15.pin15
  N81: IC14.pin3, R11.Pin_0
  N82: IC15.pin3, R10.Pin_0
  N83: IC18.pin1, IC20.pin1
  N84: IC18.pin2, IC20.pin2
  N85: IC18.pin4, IC20.pin4
  N86: IC18.pin5, IC20.pin5
  N87: IC18.pin12, IC20.pin12
  N88: IC18.pin13, IC20.pin13
  N89: IC18.pin14, IC20.pin14
  N90: IC18.pin15, IC20.pin15
  N91: IC19.pin1, IC21.pin1
  N92: IC19.pin2, IC21.pin2
  N93: IC19.pin4, IC21.pin4
  N94: IC19.pin5, IC21.pin5
  N95: IC19.pin12, IC21.pin12
  N96: IC19.pin13, IC21.pin13
  N97: IC19.pin14, IC21.pin14
  N98: IC19.pin15, IC21.pin15
  N99: IC20.pin3, R13.Pin_0
  N100: IC21.pin3, R12.Pin_0

custom parts:
  DIP - 16 pins: A DIP stand-in part for whatever IC you want. With 16 pins on a 300mil dual inline package (DIP) footprint.
